# Fritzing sketch Atlas (saved by Fritzing 0.9.3b)
breadboards: 1

parts:
  Part1 = Arduino Mega ADK (Rev3)
  Joint_2 = Molex Picoblade Series Header [package=Picoblade-53398-0271]
  Joint_3 = Molex Picoblade Series Header [part_number=0533980271 package=Picoblade-53398-0271]
  Joint_7 = Molex Picoblade Series Header [part_number=0533980371 package=Picoblade-53398-0371]
  Joint_4 = Molex Picoblade Series Header [part_number=0532610419 package=Picoblade-53261-0419]
  Joint_5 = Molex Picoblade Series Header [part_number=0532610419 package=Picoblade-53261-0419]
  Joint_6 = Molex Picoblade Series Header [part_number=0533980371 package=Picoblade-53398-0371]
  Joint_1 = Molex Picoblade Series Header [part_number=0532610419 package=Picoblade-53261-0419]
  Front_Left_Motors = DC Motor
  Back_Left_Motors = DC Motor
  Front_Right_Motors = DC Motor
  Back_Right_Motors = DC Motor
  ReImage_as_Sabertooth_2x60_ESC = VNH2SP30 [package=vnh2sp30]

nets:
  N1: Part1.A0, Joint_1.1
  N2: Part1.D18/TX1, ReImage_as_Sabertooth_2x60_ESC.PWM
  N3: Part1.D2_PWM, Joint_5.1
  N4: Part1.D3_PWM, Joint_4.1
  N5: Part1.D4_PWM, Joint_2.1
  N6: Part1.D5_PWM, Joint_3.1
  N7: Part1.D29, Joint_1.2
  N8: Part1.D30, Joint_1.3
  N9: Part1.D31, Joint_1.4
  N10: Part1.D32, Joint_4.2
  N11: Part1.D35, Joint_4.3
  N12: Part1.D36, Joint_4.4
  N13: Part1.D38, Joint_5.4
  N14: Part1.D39, Joint_5.3
  N15: Part1.D40, Joint_5.2
  N16: Part1.D42, Joint_6.3
  N17: Part1.D43, Joint_6.2
  N18: Part1.D44, Joint_6.1
  N19: Part1.D46, Joint_7.3
  N20: Part1.D47, Joint_7.2
  N21: Part1.D48, Joint_7.1
  N22: Front_Left_Motors.pin_1, Back_Left_Motors.pin_1, ReImage_as_Sabertooth_2x60_ESC.OUTA
  N23: Front_Left_Motors.pin_2, Back_Left_Motors.pin_2, ReImage_as_Sabertooth_2x60_ESC.GNDA
  N24: Front_Right_Motors.pin_1, Back_Right_Motors.pin_1, ReImage_as_Sabertooth_2x60_ESC.OUTB
  N25: Front_Right_Motors.pin_2, Back_Right_Motors.pin_2, ReImage_as_Sabertooth_2x60_ESC.GNDB
