# Fritzing sketch Sabertooth_setup (saved by Fritzing 0.9.3b)
breadboards: 1

parts:
  MD03A1 = Sabertooth 2X60 [part_number=MD03A]
  IC1 = IC, DIP package, 8 pins [chip_label=IC]
  MD03A2 = Sabertooth 2X60 [part_number=MD03A]

nets:
  N1: MD03A1.OUT_1A, IC1.pin1
  N2: MD03A1.OUT_1B, IC1.pin2
  N3: IC1.pin3, MD03A2.OUT_1A
  N4: IC1.pin4, MD03A2.OUT_1B

notes:
  Arm Sabertooth
  Mobility Sabertooth

custom parts:
  Sabertooth 2X60: The Pololu dual high-power motor driver carrier for the VNH2SP30 motor driver integrated circuits from ST. http://www.pololu.com/catalog/product/708
